# Fritzing sketch Transmitter (saved by Fritzing 0.9.2b)
breadboards: 1

parts:
  Part1 = Arduino Uno (Rev3)
  LED1 = smd LED [color="Green (555nm)" package="0805 [SMD]"]
  U2 = RF-LINK_TX [package=rf-link_tx]  # not connected

nets:
  N1: Part1.D13/SCK, LED1.anode
  N2: Part1.GND, LED1.cathode

custom parts:
  RF-LINK_TX: Common RF transmitter of the 315.00Mhz varity
